// Logisim project 3.1_Comp4.circ as structural Verilog: 4 circuits, main circuit main
module main (
  input  in_1,
  input  in_2,
  output A_B,
  output A_B_2,
  output A_B_3,
  output out_6,
  output out_7,
  output out_8,
  output out_9,
  output out_10,
  output out_11
);

  wire [3:0] A_out, B_out;

  Slider #(.width(4)) A (.out(A_out));
  Slider #(.width(4)) B (.out(B_out));
  // Probe on A_out
  // Probe on B_out
  Comp4nat comp4nat_1 (.A_B(out_8), .A_B_2(out_7), .A_B_3(out_6), .A(A_out), .B(B_out));
  // Probe on A_out
  // Probe on B_out
  Comp4ent comp4ent_1 (.A_B(out_11), .A_B_2(out_10), .A_B_3(out_9), .A(A_out), .B(B_out));
  xnor xnor_1 (A_B_2, A_B, A_B_3);
  Comp1bit comp1bit_1 (.a(in_1), .b(in_2), .Cin(2'b00), .Cout({A_B_3, A_B}));
endmodule

module Comp1bit (
  input  a,
  input  b,
  input  [1:0] Cin,
  output [1:0] Cout
);

  wire and_1_out, and_2_out, nor_1_out, nor_2_out, nor_3_out, nor_4_out, not_1_out, not_2_out, not_3_out,
       not_4_out, not_5_out, not_6_out, not_7_out, not_8_out, or_1_out, or_2_out;

  not not_1 (not_1_out, a);
  not not_2 (not_2_out, b);
  nor nor_1 (nor_1_out, not_1_out, b);
  nor nor_2 (nor_2_out, a, not_2_out);
  not not_3 (not_3_out, Cin[0]);
  nor nor_3 (nor_3_out, not_3_out, Cin[1]);
  nor nor_4 (nor_4_out, Cin[0], not_4_out);
  not not_4 (not_4_out, Cin[1]);
  not not_5 (not_5_out, nor_1_out);
  not not_6 (not_6_out, nor_2_out);
  or or_1 (or_1_out, nor_1_out, and_1_out);
  and and_1 (and_1_out, not_5_out, nor_3_out);
  or or_2 (or_2_out, nor_2_out, and_2_out);
  and and_2 (and_2_out, not_6_out, nor_4_out);
  not not_7 (not_7_out, nor_2_out);
  and and_3 (Cout[0], not_7_out, or_1_out);
  and and_4 (Cout[1], or_2_out, not_8_out);
  not not_8 (not_8_out, nor_1_out);
endmodule

module Comp4nat (
  input  [3:0] A,
  input  [3:0] B,
  output A_B,
  output A_B_2,
  output A_B_3
);

  wire [1:0] bit0_cout, bit1_cout, bit2_cout;

  Comp1bit bit3 (.a(A[3]), .b(B[3]), .Cin(bit2_cout), .Cout({A_B_3, A_B}));
  xnor xnor_1 (A_B_2, A_B, A_B_3);
  Comp1bit bit1 (.a(A[1]), .b(B[1]), .Cin(bit0_cout), .Cout(bit1_cout));
  Comp1bit bit2 (.a(A[2]), .b(B[2]), .Cin(bit1_cout), .Cout(bit2_cout));
  Comp1bit bit0 (.a(A[0]), .b(B[0]), .Cin(2'b00), .Cout(bit0_cout));
endmodule

module Comp4ent (
  input  [3:0] A,
  input  [3:0] B,
  output A_B,
  output A_B_2,
  output A_B_3
);

  wire [1:0] bit0_cout, bit1_cout, bit2_cout;

  Comp1bit bit3 (.a(B[3]), .b(A[3]), .Cin(bit2_cout), .Cout({A_B_3, A_B}));
  Comp1bit bit2 (.a(A[2]), .b(B[2]), .Cin(bit1_cout), .Cout(bit2_cout));
  xnor xnor_1 (A_B_2, A_B, A_B_3);
  Comp1bit bit1 (.a(A[1]), .b(B[1]), .Cin(bit0_cout), .Cout(bit1_cout));
  Comp1bit bit0 (.a(A[0]), .b(B[0]), .Cin(2'b00), .Cout(bit0_cout));

  // Notes on the sheet:
  //   Sa
  //   Sb
endmodule
