// Logisim project BancRegsBiport+PC.circ as structural Verilog: 4 circuits, main circuit main
module main (
  input  Write,
  input  Load,
  input  Increment,
  output Overflow
);

  wire Reset_2_out, Reset_out, Sincro_2_out, Sincro_out;
  wire [1:0] in_out, out1_out, out2_out;
  wire [7:0] bancregistres4x8b_1_regout1, bancregistres4x8b_1_regout2, Data_in_out, New_PC_value_out,
       pc8bits_1_pcout;

  Slider #(.width(2)) out1 (.out(out1_out));
  Slider #(.width(2)) out2 (.out(out2_out));
  Button Sincro (.out(Sincro_out));
  Slider Data_in (.out(Data_in_out));
  Slider #(.width(2)) in (.out(in_out));
  BancRegistres4x8b bancregistres4x8b_1 (
    .RegIn(Data_in_out), .\NúmRegIn (in_out), .Wr(Write), .Sinc(Sincro_2_out), .Reset(Reset_out),
    .RegOut1(bancregistres4x8b_1_regout1), .RegOut2(bancregistres4x8b_1_regout2), .\NúmRegOut2 (out2_out),
    .\NúmRegOut1 (out1_out));
  Button Sincro_2 (.out(Sincro_2_out));
  Button Reset (.out(Reset_out));
  Slider New_PC_value (.out(New_PC_value_out));
  PC8bits pc8bits_1 (
    .NewPC(New_PC_value_out), .Load(Load), .Inc(Increment), .Sinc(Sincro_out), .Reset(Reset_2_out),
    .PCout(pc8bits_1_pcout), .Overflow(Overflow));
  // Probe on pc8bits_1_pcout
  // Probe on bancregistres4x8b_1_regout2
  // Probe on bancregistres4x8b_1_regout1
  Button Reset_2 (.out(Reset_2_out));
endmodule

module BancRegistres4x8b (
  input  [7:0] RegIn,
  input  Wr,
  input  [1:0] \NúmRegIn ,
  input  Reset,
  input  Sinc,
  input  [1:0] \NúmRegOut1 ,
  input  [1:0] \NúmRegOut2 ,
  output [7:0] RegOut1,
  output [7:0] RegOut2
);

  wire demultiplexer_1_out0, demultiplexer_1_out1, demultiplexer_1_out2, demultiplexer_1_out3;
  wire [7:0] R0_dout, R1_dout, R2_dout, R3_dout;

  Demultiplexer #(.select(2), .enable("false")) demultiplexer_1 (
    .out0(demultiplexer_1_out0), .out1(demultiplexer_1_out1), .out2(demultiplexer_1_out2),
    .out3(demultiplexer_1_out3), .in(Wr), .sel(\NúmRegIn ));
  Registre8bits R0 (.Wr(demultiplexer_1_out0), .Sinc(Sinc), .Reset(Reset), .Din(RegIn), .Dout(R0_dout));
  Registre8bits R1 (.Wr(demultiplexer_1_out1), .Sinc(Sinc), .Reset(Reset), .Din(RegIn), .Dout(R1_dout));
  Registre8bits R2 (.Wr(demultiplexer_1_out2), .Sinc(Sinc), .Reset(Reset), .Din(RegIn), .Dout(R2_dout));
  Registre8bits R3 (.Wr(demultiplexer_1_out3), .Sinc(Sinc), .Reset(Reset), .Din(RegIn), .Dout(R3_dout));
  Multiplexer #(.select(2), .width(8), .enable("false")) multiplexer_1 (
    .in0(R0_dout), .in1(R1_dout), .in2(R2_dout), .in3(R3_dout), .out(RegOut1), .sel(\NúmRegOut1 ));
  Multiplexer #(.select(2), .width(8), .enable("false")) multiplexer_2 (
    .in0(R0_dout), .in1(R1_dout), .in2(R2_dout), .in3(R3_dout), .out(RegOut2), .sel(\NúmRegOut2 ));
endmodule

module PC8bits (
  input  [7:0] NewPC,
  input  Load,
  input  Reset,
  input  Inc,
  input  Sinc,
  output Overflow,
  output [7:0] PCout
);

  wire xor_1_out;
  wire [7:0] adder_1_out, multiplexer_1_out;

  xor xor_1 (xor_1_out, Load, Inc);
  Multiplexer #(.width(8), .enable("false")) multiplexer_1 (
    .in0(adder_1_out), .in1(NewPC), .out(multiplexer_1_out), .sel(Load));
  Registre8bits registre8bits_1 (.Wr(xor_1_out), .Sinc(Sinc), .Reset(Reset), .Din(multiplexer_1_out), .Dout(PCout));
  Adder adder_1 (.a(8'h1), .b(PCout), .out(adder_1_out), .cout(Overflow));  // open: cin
endmodule

module Registre8bits (
  input  [7:0] Din,
  input  Wr,
  input  Sinc,
  input  Reset,
  output [7:0] Dout
);

  Register #(.Select("low")) Reg8b (.D(Din), .en(Wr), .Q(Dout), .clk(Sinc), .clr(Reset));
endmodule
